# Fritzing sketch F1Wheel (saved by Fritzing 0.9.5d)

parts:
  Pro_Micro1 = SparkFun Pro Micro
  S1 = Round Pushbutton  # not connected
  S2 = Round Pushbutton  # not connected
  S3 = Round Pushbutton  # not connected
  S4 = Round Pushbutton  # not connected
  S5 = Round Pushbutton  # not connected
  S6 = Round Pushbutton  # not connected
  S7 = Round Pushbutton
  S8 = Round Pushbutton
  S9 = Round Pushbutton
  S10 = Round Pushbutton
  S11 = Round Pushbutton
  S12 = Round Pushbutton
  S13 = Square Pushbutton
  S14 = Square Pushbutton
  S15 = Square Pushbutton
  S16 = Square Pushbutton

nets:
  N1: Pro_Micro1.GND, S13.leg0
  N2: Pro_Micro1.5, S14.leg1
  N3: Pro_Micro1.6, S16.leg1
  N4: Pro_Micro1.7, S15.leg1
  N5: S7.leg1, S10.leg0
  N6: S8.leg1, S11.leg0
  N7: S9.leg1, S12.leg0

custom parts:
  SparkFun Pro Micro: The Pro Micro is similar to the Pro Mini except with an ATmega32U4 on board. The USB transceiver inside the 32U4 allows us to add USB connectivity on-board and do away with bulky external USB interface. Based on: https://github.com/unorthodox-engineers/unorthodox-arduino/blob/master/Unorthodox/fritzing/parts/Pro%20Micro.fzpz
